// Logisim project td4.circ as structural Verilog: 1 circuit, main circuit main
module main (
);

  wire adder_1_cout, button_1_out, button_2_out, button_3_out, button_4_out, button_5_out, button_6_out,
       button_7_out, button_8_out, button_9_out, button_10_out, button_11_out, button_12_out, button_13_out,
       button_14_out, button_15_out, clock_1_out, d_ff_1_q, multiplexer_1_out, nand_1_out, nand_2_out,
       not_1_out, not_2_out, not_CF, or_2_out, or_3_out, or_4_out, t_ff_13_q;
  wire [1:0] data_selector;
  wire [3:0] A_reg, B_reg, data_bus, I_N, in_data_bus, LOAD, multiplexer_2_out, O_U_T, PC;
  wire [7:0] t_ff_1_q;
  wire [7:4] rom_1_data;

  T_Flip_Flop t_ff_1 (.T(button_1_out), .clk(button_1_out), .Q(t_ff_1_q[0]));  // open: Qn, reset, preset
  Button button_1 (.out(button_1_out));
  T_Flip_Flop t_ff_2 (.T(button_2_out), .clk(button_2_out), .Q(t_ff_1_q[1]));  // open: Qn, reset, preset
  Button button_2 (.out(button_2_out));
  T_Flip_Flop t_ff_3 (.T(button_3_out), .clk(button_3_out), .Q(t_ff_1_q[2]));  // open: Qn, reset, preset
  Button button_3 (.out(button_3_out));
  T_Flip_Flop t_ff_4 (.T(button_4_out), .clk(button_4_out), .Q(t_ff_1_q[3]));  // open: Qn, reset, preset
  Button button_4 (.out(button_4_out));
  T_Flip_Flop t_ff_5 (.T(button_5_out), .clk(button_5_out), .Q(t_ff_1_q[4]));  // open: Qn, reset, preset
  Button button_5 (.out(button_5_out));
  T_Flip_Flop t_ff_6 (.T(button_6_out), .clk(button_6_out), .Q(t_ff_1_q[5]));  // open: Qn, reset, preset
  Button button_6 (.out(button_6_out));
  T_Flip_Flop t_ff_7 (.T(button_7_out), .clk(button_7_out), .Q(t_ff_1_q[6]));  // open: Qn, reset, preset
  Button button_7 (.out(button_7_out));
  T_Flip_Flop t_ff_8 (.T(button_8_out), .clk(button_8_out), .Q(t_ff_1_q[7]));  // open: Qn, reset, preset
  Button button_8 (.out(button_8_out));
  T_Flip_Flop t_ff_9 (.T(button_9_out), .clk(button_9_out), .Q(I_N[0]));  // open: Qn, reset, preset
  Button button_9 (.out(button_9_out));
  T_Flip_Flop t_ff_10 (.T(button_10_out), .clk(button_10_out), .Q(I_N[1]));  // open: Qn, reset, preset
  Button button_10 (.out(button_10_out));
  T_Flip_Flop t_ff_11 (.T(button_11_out), .clk(button_11_out), .Q(I_N[2]));  // open: Qn, reset, preset
  Button button_11 (.out(button_11_out));
  T_Flip_Flop t_ff_12 (.T(button_12_out), .clk(button_12_out), .Q(I_N[3]));  // open: Qn, reset, preset
  Button button_12 (.out(button_12_out));
  ROM #(.addrWidth(4)) rom_1 (.addr(PC), .data({rom_1_data[7:6], data_selector[1], rom_1_data[4], in_data_bus}));
  Button button_13 (.out(button_13_out));
  Multiplexer multiplexer_1 (.in0(button_14_out), .in1(clock_1_out), .out(multiplexer_1_out), .sel(t_ff_13_q));
  Button button_14 (.out(button_14_out));
  Clock clock_1 (.out(clock_1_out));
  Counter #(.max('hf), .width(4)) counter_1 (
    .clr(button_13_out), .load(LOAD[3]), .up(1'b1), .count(1'b1), .clk(multiplexer_1_out), .D(data_bus),
    .Q(PC));  // open: carry
  or or_1 (data_selector[0], rom_1_data[4], rom_1_data[7]);
  Register #(.width(4)) register_1 (
    .D(data_bus), .en(LOAD[0]), .clk(multiplexer_1_out), .Q(A_reg), .clr(button_13_out));
  Register #(.width(4)) register_2 (
    .D(data_bus), .en(LOAD[1]), .clk(multiplexer_1_out), .Q(B_reg), .clr(button_13_out));
  Register #(.width(4)) register_3 (
    .D(data_bus), .en(LOAD[2]), .clk(multiplexer_1_out), .Q(O_U_T), .clr(button_13_out));
  T_Flip_Flop t_ff_13 (.T(button_15_out), .clk(button_15_out), .Q(t_ff_13_q));  // open: Qn, reset, preset
  Button button_15 (.out(button_15_out));
  not not_1 (not_1_out, rom_1_data[6]);
  not not_2 (not_2_out, rom_1_data[6]);
  or or_2 (or_2_out, not_CF, rom_1_data[4]);
  or or_3 (or_3_out, rom_1_data[7], rom_1_data[6]);
  or or_4 (or_4_out, rom_1_data[7], not_1_out);
  nand nand_1 (nand_1_out, rom_1_data[7], not_2_out);
  nand nand_2 (nand_2_out, rom_1_data[7], rom_1_data[6], or_2_out);
  not not_3 (LOAD[0], or_3_out);
  not not_4 (LOAD[1], or_4_out);
  not not_5 (LOAD[2], nand_1_out);
  not not_6 (LOAD[3], nand_2_out);
  Multiplexer #(.select(2)) multiplexer_2 (
    .in0(A_reg[0]), .in1(B_reg[0]), .in2(I_N[0]), .in3(1'b0), .out(multiplexer_2_out[0]), .sel(data_selector));
  Multiplexer #(.select(2)) multiplexer_3 (
    .in0(A_reg[1]), .in1(B_reg[1]), .in2(I_N[1]), .in3(1'b0), .out(multiplexer_2_out[1]), .sel(data_selector));
  Multiplexer #(.select(2)) multiplexer_4 (
    .in0(A_reg[2]), .in1(B_reg[2]), .in2(I_N[2]), .in3(1'b0), .out(multiplexer_2_out[2]), .sel(data_selector));
  Multiplexer #(.select(2)) multiplexer_5 (
    .in0(A_reg[3]), .in1(B_reg[3]), .in2(I_N[3]), .in3(1'b0), .out(multiplexer_2_out[3]), .sel(data_selector));
  Adder #(.width(4)) adder_1 (
    .a(multiplexer_2_out), .b(in_data_bus), .out(data_bus), .cout(adder_1_cout));  // open: cin
  D_Flip_Flop d_ff_1 (
    .D(adder_1_cout), .clk(multiplexer_1_out), .Q(d_ff_1_q), .Qn(not_CF), .reset(button_13_out));  // open: preset

  // Notes on the sheet:
  //   Instrument for debug
  //   D0
  //   D1
  //   D2
  //   D3
  //   D4
  //   D5
  //   D6
  //   D7
  //   IN
  //   contents of rom_1 (hex, n*v repeats v):
  //   20 0 f e7 5f f2 0 5f 90 f0
  //   load
  //   TD4
  //   data bus
  //   reset
  //   clock
  //   A
  //   B
  //   manual/auto mode
  //   0-manual 1-auto
  //   L0
  //   L1
  //   L2
  //   OUT
  //   PC
  //   L3
  //   A register
  //   B register
  //   CF
endmodule
