// Logisim project td4m.circ as structural Verilog: 1 circuit, main circuit main
module main (
);

  wire adder_1_cout, and_1_out, and_2_out, button_1_out, button_2_out, button_3_out, button_4_out,
       button_5_out, button_6_out, button_7_out, button_8_out, button_9_out, button_10_out, button_11_out,
       button_12_out, button_13_out, button_14_out, d_ff_1_q, nand_1_out, nand_2_out, not_1_out, not_2_out,
       not_3_out, not_4_out, not_CF, or_2_out, or_3_out, or_4_out, or_5_out;
  wire [1:0] data_selector;
  wire [3:0] A_reg, B_reg, data_bus, I_N, in_data_bus, LOAD, multiplexer_1_out, O_U_T;
  wire [7:0] PC, XY;
  wire [7:4] t_ff_9_q;

  RAM #(.addrWidth(4), .dataWidth(1)) ram_1 ();  // open: addr, we, oe, clk, din, dout
  T_Flip_Flop t_ff_1 (.T(button_1_out), .clk(button_1_out), .Q(I_N[0]));  // open: Qn, reset, preset
  Button button_1 (.out(button_1_out));
  T_Flip_Flop t_ff_2 (.T(button_2_out), .clk(button_2_out), .Q(I_N[1]));  // open: Qn, reset, preset
  Button button_2 (.out(button_2_out));
  T_Flip_Flop t_ff_3 (.T(button_3_out), .clk(button_3_out), .Q(I_N[2]));  // open: Qn, reset, preset
  Button button_3 (.out(button_3_out));
  T_Flip_Flop t_ff_4 (.T(button_4_out), .clk(button_4_out), .Q(I_N[3]));  // open: Qn, reset, preset
  Button button_4 (.out(button_4_out));
  ROM rom_1 ();  // open: addr, data
  Button button_5 (.out(button_5_out));
  Button button_6 (.out(button_6_out));
  Button button_7 (.out(button_7_out));
  Button button_8 (.out(button_8_out));
  Button button_9 (.out(button_9_out));
  Button button_10 (.out(button_10_out));
  Button button_11 (.out(button_11_out));
  Button button_12 (.out(button_12_out));
  T_Flip_Flop t_ff_5 (.T(button_5_out), .clk(button_5_out), .Q(in_data_bus[0]));  // open: Qn, reset, preset
  T_Flip_Flop t_ff_6 (.T(button_6_out), .clk(button_6_out), .Q(in_data_bus[1]));  // open: Qn, reset, preset
  T_Flip_Flop t_ff_7 (.T(button_7_out), .clk(button_7_out), .Q(in_data_bus[2]));  // open: Qn, reset, preset
  T_Flip_Flop t_ff_8 (.T(button_8_out), .clk(button_8_out), .Q(in_data_bus[3]));  // open: Qn, reset, preset
  T_Flip_Flop t_ff_9 (.T(button_9_out), .clk(button_9_out), .Q(t_ff_9_q[4]));  // open: Qn, reset, preset
  T_Flip_Flop t_ff_10 (.T(button_10_out), .clk(button_10_out), .Q(data_selector[1]));  // open: Qn, reset, preset
  T_Flip_Flop t_ff_11 (.T(button_11_out), .clk(button_11_out), .Q(t_ff_9_q[6]));  // open: Qn, reset, preset
  T_Flip_Flop t_ff_12 (.T(button_12_out), .clk(button_12_out), .Q(t_ff_9_q[7]));  // open: Qn, reset, preset
  Button button_13 (.out(button_13_out));
  or or_1 (data_selector[0], t_ff_9_q[4], t_ff_9_q[7]);
  Button button_14 (.out(button_14_out));
  not not_1 (not_1_out, t_ff_9_q[4]);
  not not_2 (not_2_out, t_ff_9_q[6]);
  Counter counter_1 (
    .clr(button_13_out), .load(LOAD[3]), .up(1'b1), .count(1'b1), .clk(button_14_out), .Q(PC));  // open: D, carry
  Counter counter_2 (.Q(XY));  // open: clr, load, up, count, clk, D, carry
  and and_1 (and_1_out, data_selector[1], t_ff_9_q[6], t_ff_9_q[7]);
  and and_2 (and_2_out, not_1_out, not_2_out, t_ff_9_q[7]);
  Register #(.width(4)) register_1 (.D(data_bus), .en(LOAD[0]), .clk(button_14_out), .Q(A_reg), .clr(button_13_out));
  Register #(.width(4)) register_2 (.D(data_bus), .en(LOAD[1]), .clk(button_14_out), .Q(B_reg), .clr(button_13_out));
  Register #(.width(4)) register_3 (.D(data_bus), .en(LOAD[2]), .clk(button_14_out), .Q(O_U_T), .clr(button_13_out));
  or or_2 (or_2_out, and_1_out, and_2_out);
  not not_3 (not_3_out, t_ff_9_q[6]);
  not not_4 (not_4_out, t_ff_9_q[6]);
  or or_3 (or_3_out, not_CF, t_ff_9_q[4]);
  or or_4 (or_4_out, t_ff_9_q[7], t_ff_9_q[6]);
  or or_5 (or_5_out, t_ff_9_q[7], not_3_out);
  nand nand_1 (nand_1_out, t_ff_9_q[7], not_4_out);
  nand nand_2 (nand_2_out, t_ff_9_q[7], t_ff_9_q[6], or_3_out);
  not not_5 (LOAD[0], or_4_out);
  not not_6 (LOAD[1], or_5_out);
  not not_7 (LOAD[2], nand_1_out);
  not not_8 (LOAD[3], nand_2_out);
  Multiplexer #(.select(2)) multiplexer_1 (
    .in0(A_reg[0]), .in1(B_reg[0]), .in2(I_N[0]), .in3(1'b0), .out(multiplexer_1_out[0]), .sel(data_selector));
  Multiplexer #(.select(2)) multiplexer_2 (
    .in0(A_reg[1]), .in1(B_reg[1]), .in2(I_N[1]), .in3(1'b0), .out(multiplexer_1_out[1]), .sel(data_selector));
  Multiplexer #(.select(2)) multiplexer_3 (
    .in0(A_reg[2]), .in1(B_reg[2]), .in2(I_N[2]), .in3(1'b0), .out(multiplexer_1_out[2]), .sel(data_selector));
  Multiplexer #(.select(2)) multiplexer_4 (
    .in0(A_reg[3]), .in1(B_reg[3]), .in2(I_N[3]), .in3(1'b0), .out(multiplexer_1_out[3]), .sel(data_selector));
  Adder #(.width(4)) adder_1 (
    .a(multiplexer_1_out), .b(in_data_bus), .out(data_bus), .cout(adder_1_cout));  // open: cin
  D_Flip_Flop d_ff_1 (
    .D(adder_1_cout), .clk(button_14_out), .Q(d_ff_1_q), .Qn(not_CF), .reset(button_13_out));  // open: preset

  // Notes on the sheet:
  //   TD4m
  //   IN
  //   D0
  //   D1
  //   D2
  //   D3
  //   D4
  //   D5
  //   D6
  //   D7
  //   load
  //   data bus
  //   reset
  //   clock
  //   A
  //   B
  //   is 0-3 command?
  //   L0
  //   L1
  //   L2
  //   OUT
  //   PC
  //   L3
  //   A register
  //   B register
  //   CF
endmodule
